// Logisim project Morse Code Converter.circ as structural Verilog: 1 circuit, main circuit main
module main (
  output [2:0] out_1
);

  wire and_1_out, and_2_out, and_4_out, and_5_out, Clear, CP, CP_2_out, CP_3_out, CP_out, d_ff_1_qn,
       d_ff_2_qn, d_ff_3_qn, No_Input_out, not_1_out, not_2_out, not_3_out, not_4_out, not_5_out, not_6_out,
       not_7_out, not_8_out, not_9_out, not_10_out, or_1_out, or_2_out, rom_1_data, rom_2_data, rom_3_data,
       rom_4_data, rom_6_data, rom_7_data, rom_8_data, rom_9_data, To_Clear_out;
  wire [1:0] comparator_1_eq, Enter_out, For_W_out, For_X_out, For_Y_out, For_Z_out, rom_5_data;
  wire [6:0] keyboard_1_data, multiplexer_1_out, multiplexer_2_out, multiplexer_3_out, multiplexer_4_out,
       multiplexer_5_out, multiplexer_6_out, multiplexer_7_out, multiplexer_8_out, multiplexer_9_out,
       multiplexer_10_out, sound_emitter_1_p3;

  Button To_Clear (.out(To_Clear_out));
  Clock #(.highDuration(6), .lowDuration(6)) u_CP (.out(CP_out));
  not not_1 (not_1_out, CP_out);
  Multiplexer #(.select(2), .width(7)) multiplexer_1 (
    .in0({7{1'b0}}), .in1(7'b0101110), .in2(7'b0101101), .in3({7{1'b0}}), .out(multiplexer_1_out),
    .sel(rom_5_data));  // open: en
  or No_Input (No_Input_out, keyboard_1_data[6], keyboard_1_data[5], keyboard_1_data[4], keyboard_1_data[3], keyboard_1_data[2], keyboard_1_data[1], keyboard_1_data[0]);
  Keyboard keyboard_1 (.clk(not_1_out), .clr(To_Clear_out), .data(keyboard_1_data));  // open: re, avail
  Multiplexer #(.select(2), .width(7)) multiplexer_2 (
    .in0({7{1'b0}}), .in1(7'b0101110), .in2(7'b0101101), .in3({7{1'b0}}), .out(multiplexer_2_out),
    .sel(For_W_out));  // open: en
  not not_2 (not_2_out, rom_5_data[0]);
  and For_V_minus (rom_5_data[1], not_2_out, No_Input_out);
  ROM #(.addrWidth(7), .dataWidth(1)) rom_1 (.addr(keyboard_1_data), .data(rom_1_data));  // open: sel
  ROM #(.addrWidth(7), .dataWidth(1)) rom_2 (.addr(keyboard_1_data), .data(rom_2_data));  // open: sel
  ROM #(.addrWidth(7), .dataWidth(1)) rom_3 (.addr(keyboard_1_data), .data(rom_3_data));  // open: sel
  ROM #(.addrWidth(7), .dataWidth(1)) rom_4 (.addr(keyboard_1_data), .data(rom_4_data));  // open: sel
  nor Space (Enter_out[1], keyboard_1_data[0], keyboard_1_data[1], keyboard_1_data[2], keyboard_1_data[3], keyboard_1_data[4], ~keyboard_1_data[5], keyboard_1_data[6]);  // NOR_Gate
  nor Enter (Enter_out[0], keyboard_1_data[0], ~keyboard_1_data[1], keyboard_1_data[2], ~keyboard_1_data[3], keyboard_1_data[4], keyboard_1_data[5], keyboard_1_data[6]);  // NOR_Gate
  ROM #(.addrWidth(7), .dataWidth(1)) rom_5 (.addr(keyboard_1_data), .data(rom_5_data[0]));  // open: sel
  ROM #(.addrWidth(7), .dataWidth(1)) rom_6 (.addr(keyboard_1_data), .data(rom_6_data));  // open: sel
  ROM #(.addrWidth(7), .dataWidth(1)) rom_7 (.addr(keyboard_1_data), .data(rom_7_data));  // open: sel
  ROM #(.addrWidth(7), .dataWidth(1)) rom_8 (.addr(keyboard_1_data), .data(rom_8_data));  // open: sel
  ROM #(.addrWidth(7), .dataWidth(1)) rom_9 (.addr(keyboard_1_data), .data(rom_9_data));  // open: sel
  Multiplexer #(.select(2), .width(7)) multiplexer_3 (
    .in0({7{1'b0}}), .in1(7'b0101110), .in2(7'b0101101), .in3({7{1'b0}}), .out(multiplexer_3_out),
    .sel(For_X_out));  // open: en
  not not_3 (not_3_out, For_W_out[0]);
  not not_4 (not_4_out, For_X_out[0]);
  not not_5 (not_5_out, For_Y_out[0]);
  not not_6 (not_6_out, rom_1_data);
  not not_7 (not_7_out, For_Z_out[0]);
  not not_8 (not_8_out, rom_2_data);
  not not_9 (not_9_out, rom_3_data);
  not not_10 (not_10_out, rom_4_data);
  or or_1 (or_1_out, and_1_out, and_2_out);
  and and_1 (and_1_out, out_1[1], out_1[0]);
  and and_2 (and_2_out, out_1[2], d_ff_3_qn);
  Multiplexer #(.select(2), .width(7)) multiplexer_4 (
    .in0({7{1'b0}}), .in1(7'b0101110), .in2(7'b0101101), .in3({7{1'b0}}), .out(multiplexer_4_out),
    .sel(For_Y_out));  // open: en
  and For_W_minus (For_W_out[1], not_6_out, not_3_out, No_Input_out);
  and For_X_minus (For_X_out[1], not_8_out, not_4_out, No_Input_out);
  and For_Y_minus (For_Y_out[1], not_9_out, No_Input_out, not_5_out);
  and For_Z_minus (For_Z_out[1], No_Input_out, not_7_out, not_10_out, not_10_out);
  or or_2 (or_2_out, and_5_out, and_4_out);
  Button To_Clear_2 (.out(Clear));
  Clock CP_2 (.out(CP_2_out));
  and and_3 (CP, No_Input_out, CP_2_out);
  and For_W (For_W_out[0], not_6_out, rom_6_data);
  D_Flip_Flop d_ff_1 (.clk(CP), .D(or_1_out), .Q(out_1[2]), .Qn(d_ff_1_qn), .reset(Clear));  // open: preset, en
  and and_4 (and_4_out, d_ff_1_qn, out_1[0], d_ff_2_qn);
  and For_X (For_X_out[0], not_8_out, rom_7_data);
  and and_5 (and_5_out, out_1[1], d_ff_3_qn);
  Multiplexer #(.select(2), .width(7)) multiplexer_5 (
    .in0({7{1'b0}}), .in1(7'b0101110), .in2(7'b0101101), .in3({7{1'b0}}), .out(multiplexer_5_out),
    .sel(For_Z_out));  // open: en
  and For_Z (For_Z_out[0], not_10_out, rom_9_data);
  and For_Y (For_Y_out[0], not_9_out, rom_8_data);
  D_Flip_Flop d_ff_2 (.clk(CP), .D(or_2_out), .Q(out_1[1]), .Qn(d_ff_2_qn), .reset(Clear));  // open: preset, en
  Multiplexer #(.select(3), .width(7)) multiplexer_6 (
    .in0(multiplexer_1_out), .in1(multiplexer_2_out), .in2(multiplexer_3_out), .in3(multiplexer_4_out),
    .in4(multiplexer_5_out), .in5(7'b0100000), .out(multiplexer_6_out), .sel(out_1));  // open: in6, in7, en
  Multiplexer #(.select(3), .width(7)) multiplexer_7 (
    .in0(7'b0001101), .in1({7{1'b0}}), .in2({7{1'b0}}), .in3({7{1'b0}}), .in4({7{1'b0}}), .in5({7{1'b0}}),
    .out(multiplexer_7_out), .sel(out_1));  // open: in6, in7, en
  Multiplexer #(.select(3), .width(7)) multiplexer_8 (
    .in0(7'b0100000), .in1({7{1'b0}}), .in2({7{1'b0}}), .in3({7{1'b0}}), .in4({7{1'b0}}), .in5({7{1'b0}}),
    .out(multiplexer_8_out), .sel(out_1));  // open: in6, in7, en
  TTY tty_1 (.data(multiplexer_9_out), .clk(CP), .clr(Clear));  // open: we
  Multiplexer #(.select(2), .width(7)) multiplexer_9 (
    .in0(multiplexer_6_out), .in1(multiplexer_7_out), .in2(multiplexer_8_out), .out(multiplexer_9_out),
    .sel(Enter_out));  // open: in3, en
  D_Flip_Flop d_ff_3 (.clk(CP), .D(d_ff_3_qn), .Q(out_1[0]), .Qn(d_ff_3_qn), .reset(Clear));  // open: preset, en
  Clock #(.highDuration(2), .lowDuration(2)) CP_3 (.out(CP_3_out));
  Comparator #(.width(7)) comparator_1 (
    .a(multiplexer_9_out), .b(7'b0101110), .eq(comparator_1_eq[0]));  // open: gt, lt
  Comparator #(.width(7)) comparator_2 (
    .a(multiplexer_9_out), .b(7'b0101101), .eq(comparator_1_eq[1]));  // open: gt, lt
  Multiplexer #(.select(2), .width(7)) multiplexer_10 (
    .in1(7'b1010101), .in2(7'b1000000), .out(multiplexer_10_out), .sel(comparator_1_eq));  // open: in0, in3, en
  // sound_emitter sound_emitter_1: pin names not known; wires that end beside it: CP_3_out, multiplexer_10_out, sound_emitter_1_p3
  Multiplexer #(.select(2), .width(7)) multiplexer_11 (
    .in0({7{1'b0}}), .in1(7'b1100100), .in2(7'b1100100), .in3({7{1'b0}}), .out(sound_emitter_1_p3),
    .sel(comparator_1_eq));  // open: en

  // Other names for the same wires on the sheet: OUT[2:0] = out_1

  // Notes on the sheet:
  //   V
  //   Input
  //   W
  //   22BCE308
  //   X
  //   contents of rom_1 (hex, n*v repeats v):
  //   69*0 1 14*0 1
  //   contents of rom_2 (hex, n*v repeats v):
  //   65*0 1 0 0 0 1 0 0 0 1 0 0 0 1 1 5*0 1
  //   contents of rom_3 (hex, n*v repeats v):
  //   65*0 1 0 0 1 1 0 1 0 1 0 1 0 1 1 1 0 0 4*1 0 1
  //   contents of rom_4 (hex, n*v repeats v):
  //   65*0 63*1
  //   contents of rom_5 (hex, n*v repeats v):
  //   49*0 5*1 11*0 1 0 0 0 1 1 0 1 1 1 0 1 0 0 0 1 0 1 1 0 1 1 1
  //   contents of rom_6 (hex, n*v repeats v):
  //   50*0 5*1 11*0 1 1 1 0 1 0 1 1 0 1 0 0 1 4*0 1 0 1 1 0 1 1
  //   contents of rom_7 (hex, n*v repeats v):
  //   51*0 5*1 10*0 1 0 1 0 0 1 1 0 0 0 1 4*0 1 1 1 0 0 1 0 1 0 1
  //   contents of rom_8 (hex, n*v repeats v):
  //   52*0 5*1 9*0 1 1 0 0 1 0 1 0 0 0 1 0 0 0 1 9*0 1
  //   contents of rom_9 (hex, n*v repeats v):
  //   53*0 5*1
  //   English/Number to Morse and Sound
  //   22BCE309
  //   Y
  //   Z
  //   Output
  //   Sound Output
endmodule
